// Digital circuit Add16.dig as structural Verilog
module Add16 (
  input  [15:0] a,
  input  [15:0] b,
  output [15:0] sum,
  output carry
);

  wire add_1_c_o, add_2_c_o, add_3_c_o, add_4_c_o, add_5_c_o, add_6_c_o, add_7_c_o, add_8_c_o, add_9_c_o,
       add_10_c_o, add_11_c_o, add_12_c_o, add_13_c_o, add_14_c_o, add_15_c_o;

  Add add_1 (.a(a[0]), .b(b[0]), .c_i(1'b0), .s(sum[0]), .c_o(add_1_c_o));
  Add add_2 (.a(a[1]), .b(b[1]), .c_i(add_1_c_o), .s(sum[1]), .c_o(add_2_c_o));
  Add add_3 (.a(a[2]), .b(b[2]), .c_i(add_2_c_o), .s(sum[2]), .c_o(add_3_c_o));
  Add add_4 (.a(a[3]), .b(b[3]), .c_i(add_3_c_o), .s(sum[3]), .c_o(add_4_c_o));
  Add add_5 (.a(a[4]), .b(b[4]), .c_i(add_4_c_o), .s(sum[4]), .c_o(add_5_c_o));
  Add add_6 (.a(a[5]), .b(b[5]), .c_i(add_5_c_o), .s(sum[5]), .c_o(add_6_c_o));
  Add add_7 (.a(a[6]), .b(b[6]), .c_i(add_6_c_o), .s(sum[6]), .c_o(add_7_c_o));
  Add add_8 (.a(a[7]), .b(b[7]), .c_i(add_7_c_o), .s(sum[7]), .c_o(add_8_c_o));
  Add add_9 (.a(a[8]), .b(b[8]), .c_i(add_8_c_o), .s(sum[8]), .c_o(add_9_c_o));
  Add add_10 (.a(a[9]), .b(b[9]), .c_i(add_9_c_o), .s(sum[9]), .c_o(add_10_c_o));
  Add add_11 (.a(a[10]), .b(b[10]), .c_i(add_10_c_o), .s(sum[10]), .c_o(add_11_c_o));
  Add add_12 (.a(a[11]), .b(b[11]), .c_i(add_11_c_o), .s(sum[11]), .c_o(add_12_c_o));
  Add add_13 (.a(a[12]), .b(b[12]), .c_i(add_12_c_o), .s(sum[12]), .c_o(add_13_c_o));
  Add add_14 (.a(a[13]), .b(b[13]), .c_i(add_13_c_o), .s(sum[13]), .c_o(add_14_c_o));
  Add add_15 (.a(a[14]), .b(b[14]), .c_i(add_14_c_o), .s(sum[14]), .c_o(add_15_c_o));
  Add add_16 (.a(a[15]), .b(b[15]), .c_i(add_15_c_o), .s(sum[15]), .c_o(carry));
endmodule
