// Digital circuit Bit.dig as structural Verilog
module Bit (
  input  load,
  input  in,
  input  c,
  output out
);

  wire multiplexer_1_out;

  Multiplexer multiplexer_1 (.sel(load), .in_0(out), .in_1(in), .out(multiplexer_1_out));
  D_FF d_ff_1 (.D(multiplexer_1_out), .C(c), .Q(out));  // open: nQ
endmodule
