// Digital circuit CPU.dig as structural Verilog
module CPU (
  input  [15:0] inM,
  input  [15:0] instruction,
  input  reset,
  input  c,
  output [15:0] outM,
  output WriteM,
  output [14:0] AddressM,
  output [14:0] PC
);

  wire and_1_out, and_2_out, and_3_out, c1, c2, c3, c4, c5, c6, CalcM, destA, destM, equal, great, less, nag,
       not_1_out, not_2_out, not_3_out, or_1_out, or_2_out, zero;
  wire [15:0] DRegister_out, multiplexer_2_out, multiplexer_3_out;
  wire [15:13] multiplexer_1_out;
  wire [15:15] ARegister_out, pc_1_out;

  Multiplexer #(.Bits(16)) multiplexer_1 (
    .sel(instruction[15]), .in_0({16{1'b0}}), .in_1(instruction),
    .out({multiplexer_1_out, CalcM, c1, c2, c3, c4, c5, c6, destA, WriteM, destM, less, equal, great}));
  not not_1 (not_1_out, instruction[15]);
  not not_2 (not_2_out, zero);
  not not_3 (not_3_out, nag);
  Multiplexer #(.Bits(16)) multiplexer_2 (.sel(not_1_out), .in_0(outM), .in_1(instruction), .out(multiplexer_2_out));
  and and_1 (and_1_out, not_2_out, not_3_out, great);
  and and_2 (and_2_out, zero, equal);
  and and_3 (and_3_out, nag, less);
  or or_1 (or_1_out, destA, not_1_out);
  or or_2 (or_2_out, and_1_out, and_2_out, and_3_out);
  Register ARegister (.load(or_1_out), .in(multiplexer_2_out), .c(c), .out({ARegister_out[15], AddressM}));
  Register DRegister (.load(WriteM), .in(outM), .c(c), .out(DRegister_out));
  Multiplexer #(.Bits(16)) multiplexer_3 (
    .sel(CalcM), .in_0({ARegister_out[15], AddressM}), .in_1(inM), .out(multiplexer_3_out));
  ALU alu_1 (
    .x(DRegister_out), .y(multiplexer_3_out), .zx(c1), .nx(c2), .zy(c3), .ny(c4), .f(c5), .no(c6),
    .out(outM), .zr(zero), .ng(nag));
  PC pc_1 (
    .inc(1'b1), .load(or_2_out), .in({ARegister_out[15], AddressM}), .reset(reset), .c(c),
    .out({pc_1_out[15], PC}));

  // Other names for the same wires on the sheet: destD = WriteM; clock = c

  // Notes on the sheet:
  //   inM: M value input  (M = contents of RAM[A])
  //   instruction: Instruction for execution
  //   reset: Signals whether to re-start the current program (reset==1) or continue executing the current program (reset==0).
  //   outM: M value output (16bit)
  //   WriteM: Write to M?
  //   AddressM: Address in data memory (of A) (15bit)
  //   PC: address of next instruction (15bit)
endmodule
