// Digital circuit Inc16.dig as structural Verilog
module Inc16 (
  input  [15:0] in_16,
  output [15:0] out_16
);

  wire [15:1] undriven;

  Add #(.Bits(16)) add_1 (.a(in_16), .b({undriven, 1'b1}), .s(out_16));  // open: c_i, c_o
  // Pins of 1 and 16 bits meet at {undriven, 1'b1}
endmodule
