// Digital circuit Memory.dig as structural Verilog
module Memory (
  input  [15:0] in,
  input  load,
  input  [14:0] address,
  input  c,
  output [15:0] out
);

  wire demultiplexer_1_out_0, demultiplexer_1_out_1, demultiplexer_1_out_2, demultiplexer_1_out_3, or_1_out;
  wire [15:0] KBD_d, RAM16K_d, SCREEN_d;

  Demultiplexer #(.Selector_Bits(2)) demultiplexer_1 (
    .sel(address[14:13]), .in(load), .out_0(demultiplexer_1_out_0), .out_1(demultiplexer_1_out_1),
    .out_2(demultiplexer_1_out_2), .out_3(demultiplexer_1_out_3));
  or or_1 (or_1_out, demultiplexer_1_out_0, demultiplexer_1_out_1);
  BlockRAMDualPort #(.AddrBits(14), .Bits(16)) RAM16K (
    .A(address[13:0]), .Din(in), .str(or_1_out), .C(c), .D(RAM16K_d));
  BlockRAMDualPort #(.AddrBits(13), .Bits(16)) SCREEN (
    .A(address[12:0]), .Din(in), .str(demultiplexer_1_out_2), .C(c), .D(SCREEN_d));
  BlockRAMDualPort #(.AddrBits(13), .Bits(16)) KBD (
    .A(address[12:0]), .Din(in), .str(demultiplexer_1_out_3), .C(c), .D(KBD_d));
  Multiplexer #(.Bits(16), .Selector_Bits(2)) multiplexer_1 (
    .sel(address[14:13]), .in_0(RAM16K_d), .in_1(RAM16K_d), .in_2(SCREEN_d), .in_3(KBD_d), .out(out));
endmodule
