// Digital circuit Or16Way.dig as structural Verilog
module Or16Way (
  input  [15:0] in_16,
  output out
);

  wire or_1_out, or_2_out;

  or or_1 (or_1_out, in_16[0], in_16[1], in_16[2], in_16[3], in_16[4], in_16[5], in_16[6], in_16[7]);
  or or_2 (or_2_out, in_16[8], in_16[9], in_16[10], in_16[11], in_16[12], in_16[13], in_16[14], in_16[15]);
  or or_3 (out, or_1_out, or_2_out);
endmodule
