// Digital circuit PC.dig as structural Verilog
// A 16-bit counter with load and reset control bits.
// if      (reset[t] == 1) out[t+1] = 0
// else if (load[t] == 1)  out[t+1] = in[t]
// else if (inc[t] == 1)   out[t+1] = out[t] + 1  (integer addition)
// else                    out[t+1] = out[t]
module PC (
  input  inc,
  input  load,
  input  [15:0] in,
  input  reset,
  input  c,
  output [15:0] out
);

  wire or_1_out;
  wire [15:0] inc16_1_out_16, multiplexer_1_out, multiplexer_2_out;

  Inc16 inc16_1 (.in_16(out), .out_16(inc16_1_out_16));
  Multiplexer #(.Bits(16)) multiplexer_1 (.sel(load), .in_0(inc16_1_out_16), .in_1(in), .out(multiplexer_1_out));
  or or_1 (or_1_out, inc, reset, load);
  Multiplexer #(.Bits(16)) multiplexer_2 (
    .sel(reset), .in_0(multiplexer_1_out), .in_1({16{1'b0}}), .out(multiplexer_2_out));
  Register register_1 (.load(or_1_out), .in(multiplexer_2_out), .c(c), .out(out));
endmodule
