// Digital circuit RAM16K.dig as structural Verilog
module RAM16K (
  input  [13:0] address,
  input  load,
  input  [15:0] in,
  input  c,
  output [15:0] out
);

  wire demultiplexer_1_out_0, demultiplexer_1_out_1, demultiplexer_1_out_2, demultiplexer_1_out_3;
  wire [15:0] ram4k_1_out, ram4k_2_out, ram4k_3_out, ram4k_4_out;

  Demultiplexer #(.Selector_Bits(2)) demultiplexer_1 (
    .sel(address[13:12]), .in(load), .out_0(demultiplexer_1_out_0), .out_1(demultiplexer_1_out_1),
    .out_2(demultiplexer_1_out_2), .out_3(demultiplexer_1_out_3));
  RAM4K ram4k_1 (.address(address[11:0]), .load(demultiplexer_1_out_0), .in(in), .c(c), .out(ram4k_1_out));
  RAM4K ram4k_2 (.address(address[11:0]), .load(demultiplexer_1_out_2), .in(in), .c(c), .out(ram4k_2_out));
  RAM4K ram4k_3 (.address(address[11:0]), .load(demultiplexer_1_out_1), .in(in), .c(c), .out(ram4k_3_out));
  RAM4K ram4k_4 (.address(address[11:0]), .load(demultiplexer_1_out_3), .in(in), .c(c), .out(ram4k_4_out));
  Multiplexer #(.Selector_Bits(2), .Bits(16)) multiplexer_1 (
    .sel(address[13:12]), .in_0(ram4k_1_out), .in_1(ram4k_3_out), .in_2(ram4k_2_out), .in_3(ram4k_4_out),
    .out(out));
endmodule
