// Digital circuit RAM4K.dig as structural Verilog
module RAM4K (
  input  [11:0] address,
  input  load,
  input  [15:0] in,
  input  c,
  output [15:0] out
);

  wire demultiplexer_1_out_0, demultiplexer_1_out_1, demultiplexer_1_out_2, demultiplexer_1_out_3,
       demultiplexer_1_out_4, demultiplexer_1_out_5, demultiplexer_1_out_6, demultiplexer_1_out_7;
  wire [15:0] ram512_1_out, ram512_2_out, ram512_3_out, ram512_4_out, ram512_5_out, ram512_6_out,
       ram512_7_out, ram512_8_out;

  Demultiplexer #(.Selector_Bits(3)) demultiplexer_1 (
    .sel(address[11:9]), .in(load), .out_0(demultiplexer_1_out_0), .out_1(demultiplexer_1_out_1),
    .out_2(demultiplexer_1_out_2), .out_3(demultiplexer_1_out_3), .out_4(demultiplexer_1_out_4),
    .out_5(demultiplexer_1_out_5), .out_6(demultiplexer_1_out_6), .out_7(demultiplexer_1_out_7));
  RAM512 ram512_1 (.address(address[8:0]), .load(demultiplexer_1_out_0), .in(in), .c(c), .out(ram512_1_out));
  RAM512 ram512_2 (.address(address[8:0]), .load(demultiplexer_1_out_2), .in(in), .c(c), .out(ram512_2_out));
  RAM512 ram512_3 (.address(address[8:0]), .load(demultiplexer_1_out_4), .in(in), .c(c), .out(ram512_3_out));
  RAM512 ram512_4 (.address(address[8:0]), .load(demultiplexer_1_out_6), .in(in), .c(c), .out(ram512_4_out));
  RAM512 ram512_5 (.address(address[8:0]), .load(demultiplexer_1_out_1), .in(in), .c(c), .out(ram512_5_out));
  RAM512 ram512_6 (.address(address[8:0]), .load(demultiplexer_1_out_3), .in(in), .c(c), .out(ram512_6_out));
  RAM512 ram512_7 (.address(address[8:0]), .load(demultiplexer_1_out_5), .in(in), .c(c), .out(ram512_7_out));
  RAM512 ram512_8 (.address(address[8:0]), .load(demultiplexer_1_out_7), .in(in), .c(c), .out(ram512_8_out));
  Multiplexer #(.Selector_Bits(3), .Bits(16)) multiplexer_1 (
    .sel(address[11:9]), .in_0(ram512_1_out), .in_1(ram512_5_out), .in_2(ram512_2_out), .in_3(ram512_6_out),
    .in_4(ram512_3_out), .in_5(ram512_7_out), .in_6(ram512_4_out), .in_7(ram512_8_out), .out(out));
endmodule
