// Digital circuit RAM64.dig as structural Verilog
module RAM64 (
  input  [5:0] address,
  input  load,
  input  [15:0] in,
  input  c,
  output [15:0] out
);

  wire demultiplexer_1_out_0, demultiplexer_1_out_1, demultiplexer_1_out_2, demultiplexer_1_out_3,
       demultiplexer_1_out_4, demultiplexer_1_out_5, demultiplexer_1_out_6, demultiplexer_1_out_7;
  wire [15:0] ram8_1_out, ram8_2_out, ram8_3_out, ram8_4_out, ram8_5_out, ram8_6_out, ram8_7_out, ram8_8_out;

  Demultiplexer #(.Selector_Bits(3)) demultiplexer_1 (
    .sel(address[5:3]), .in(load), .out_0(demultiplexer_1_out_0), .out_1(demultiplexer_1_out_1),
    .out_2(demultiplexer_1_out_2), .out_3(demultiplexer_1_out_3), .out_4(demultiplexer_1_out_4),
    .out_5(demultiplexer_1_out_5), .out_6(demultiplexer_1_out_6), .out_7(demultiplexer_1_out_7));
  RAM8 ram8_1 (.address(address[2:0]), .load(demultiplexer_1_out_0), .in(in), .c(c), .out(ram8_1_out));
  RAM8 ram8_2 (.address(address[2:0]), .load(demultiplexer_1_out_2), .in(in), .c(c), .out(ram8_2_out));
  RAM8 ram8_3 (.address(address[2:0]), .load(demultiplexer_1_out_4), .in(in), .c(c), .out(ram8_3_out));
  RAM8 ram8_4 (.address(address[2:0]), .load(demultiplexer_1_out_6), .in(in), .c(c), .out(ram8_4_out));
  RAM8 ram8_5 (.address(address[2:0]), .load(demultiplexer_1_out_1), .in(in), .c(c), .out(ram8_5_out));
  RAM8 ram8_6 (.address(address[2:0]), .load(demultiplexer_1_out_3), .in(in), .c(c), .out(ram8_6_out));
  RAM8 ram8_7 (.address(address[2:0]), .load(demultiplexer_1_out_5), .in(in), .c(c), .out(ram8_7_out));
  RAM8 ram8_8 (.address(address[2:0]), .load(demultiplexer_1_out_7), .in(in), .c(c), .out(ram8_8_out));
  Multiplexer #(.Selector_Bits(3), .Bits(16)) multiplexer_1 (
    .sel(address[5:3]), .in_0(ram8_1_out), .in_1(ram8_5_out), .in_2(ram8_2_out), .in_3(ram8_6_out),
    .in_4(ram8_3_out), .in_5(ram8_7_out), .in_6(ram8_4_out), .in_7(ram8_8_out), .out(out));
endmodule
