// Digital circuit RAM8.dig as structural Verilog
module RAM8 (
  input  [2:0] address,
  input  load,
  input  [15:0] in,
  input  c,
  output [15:0] out
);

  wire demultiplexer_1_out_0, demultiplexer_1_out_1, demultiplexer_1_out_2, demultiplexer_1_out_3,
       demultiplexer_1_out_4, demultiplexer_1_out_5, demultiplexer_1_out_6, demultiplexer_1_out_7;
  wire [15:0] register_1_out, register_2_out, register_3_out, register_4_out, register_5_out, register_6_out,
       register_7_out, register_8_out;

  Demultiplexer #(.Selector_Bits(3)) demultiplexer_1 (
    .sel(address), .in(load), .out_0(demultiplexer_1_out_0), .out_1(demultiplexer_1_out_1),
    .out_2(demultiplexer_1_out_2), .out_3(demultiplexer_1_out_3), .out_4(demultiplexer_1_out_4),
    .out_5(demultiplexer_1_out_5), .out_6(demultiplexer_1_out_6), .out_7(demultiplexer_1_out_7));
  Register register_1 (.load(demultiplexer_1_out_0), .in(in), .c(c), .out(register_1_out));
  Register register_2 (.load(demultiplexer_1_out_1), .in(in), .c(c), .out(register_2_out));
  Register register_3 (.load(demultiplexer_1_out_2), .in(in), .c(c), .out(register_3_out));
  Register register_4 (.load(demultiplexer_1_out_3), .in(in), .c(c), .out(register_4_out));
  Register register_5 (.load(demultiplexer_1_out_4), .in(in), .c(c), .out(register_5_out));
  Register register_6 (.load(demultiplexer_1_out_5), .in(in), .c(c), .out(register_6_out));
  Register register_7 (.load(demultiplexer_1_out_6), .in(in), .c(c), .out(register_7_out));
  Register register_8 (.load(demultiplexer_1_out_7), .in(in), .c(c), .out(register_8_out));
  Multiplexer #(.Selector_Bits(3), .Bits(16)) multiplexer_1 (
    .sel(address), .in_0(register_1_out), .in_1(register_2_out), .in_2(register_3_out),
    .in_3(register_4_out), .in_4(register_5_out), .in_5(register_6_out), .in_6(register_7_out),
    .in_7(register_8_out), .out(out));
endmodule
