// Digital circuit Register.dig as structural Verilog
module Register (
  input  load,
  input  [15:0] in,
  input  c,
  output [15:0] out
);

  Bit bit_1 (.load(load), .in(in[0]), .c(c), .out(out[0]));
  Bit bit_2 (.load(load), .in(in[15]), .c(c), .out(out[15]));
  Bit bit_3 (.load(load), .in(in[1]), .c(c), .out(out[1]));
  Bit bit_4 (.load(load), .in(in[14]), .c(c), .out(out[14]));
  Bit bit_5 (.load(load), .in(in[2]), .c(c), .out(out[2]));
  Bit bit_6 (.load(load), .in(in[13]), .c(c), .out(out[13]));
  Bit bit_7 (.load(load), .in(in[3]), .c(c), .out(out[3]));
  Bit bit_8 (.load(load), .in(in[4]), .c(c), .out(out[4]));
  Bit bit_9 (.load(load), .in(in[12]), .c(c), .out(out[12]));
  Bit bit_10 (.load(load), .in(in[11]), .c(c), .out(out[11]));
  Bit bit_11 (.load(load), .in(in[5]), .c(c), .out(out[5]));
  Bit bit_12 (.load(load), .in(in[10]), .c(c), .out(out[10]));
  Bit bit_13 (.load(load), .in(in[6]), .c(c), .out(out[6]));
  Bit bit_14 (.load(load), .in(in[9]), .c(c), .out(out[9]));
  Bit bit_15 (.load(load), .in(in[7]), .c(c), .out(out[7]));
  Bit bit_16 (.load(load), .in(in[8]), .c(c), .out(out[8]));
endmodule
